# Fritzing sketch env-monitor (saved by Fritzing 0.7.10b)
breadboards: 1

parts:
  Arduino1 = Arduino
  R1 = Photocell (LDR) [package=THT]
  T1 = LM34 Temperature Sensor [package="TO92 [THT]"]
  R2 = Resistor [tolerance=±5% resistance=100 package=THT]

nets:
  GND: Arduino1.GND, T1.GND, R2.Pin_0
  N1: Arduino1.3V3, R1.pin_1, T1.+Vs
  N2: Arduino1.A0, R1.pin_0, R2.Pin_1
  N3: Arduino1.A1, T1.Vout
